# Fritzing sketch Untitled Sketch (saved by Fritzing 0.9.3b)

parts:
  Arduino_Nano = Arduino Nano (Rev3.0)
  L298N_Motors_Controller = L298N DC motor driver
  Part2 = Pololu 3.3V Step-Up Voltage Regulator U1V11F3
  Part3 = Pololu 3.3V Step-Up Voltage Regulator U1V11F3
  UBEC_Voltage_Regulator = LM2596 step down module
  7_4_LiPO_Battery = LIPO-1000mAh [package=lipo-1000]
  HC_05_Bluetooth_Module = Bluetooth HC-05 Macho
  L298N_Weapon_Controller = L298N DC motor driver
  Weapon_Motor = DC Motor
  KY_031_Right_Hit_Sensor = TTP223B Capacitive Touch Sensor Module
  KY031_Left_Hit_Sensor = TTP223B Capacitive Touch Sensor Module
  Zero_Bot_Servo_Weapon = Basic Servo

nets:
  N1: Arduino_Nano.D1/TX, KY031_Left_Hit_Sensor.SIG
  N2: Arduino_Nano.D0/RX, KY_031_Right_Hit_Sensor.SIG
  N3: Arduino_Nano.D2, L298N_Motors_Controller.IN1
  N4: Arduino_Nano.D3, L298N_Motors_Controller.IN2
  N5: Arduino_Nano.D4, L298N_Motors_Controller.IN3
  N6: Arduino_Nano.D5, L298N_Motors_Controller.IN4
  N7: Arduino_Nano.D8, HC_05_Bluetooth_Module.RXD
  N8: Arduino_Nano.D9, HC_05_Bluetooth_Module.TXD
  N9: Arduino_Nano.D10, L298N_Weapon_Controller.IN1, Zero_Bot_Servo_Weapon.pulse
  VCC: Arduino_Nano.VIN, L298N_Motors_Controller.12V, UBEC_Voltage_Regulator.OUT+, HC_05_Bluetooth_Module.VCC, L298N_Weapon_Controller.12V, KY_031_Right_Hit_Sensor.VCC, KY031_Left_Hit_Sensor.VCC
  GND: Arduino_Nano.GND, L298N_Motors_Controller.GND, UBEC_Voltage_Regulator.IN-, UBEC_Voltage_Regulator.OUT-, 7_4_LiPO_Battery.-, HC_05_Bluetooth_Module.GND, L298N_Weapon_Controller.GND, KY_031_Right_Hit_Sensor.GND, KY031_Left_Hit_Sensor.GND, Zero_Bot_Servo_Weapon.gnd
  N10: L298N_Motors_Controller.OUT1, Part3.IN2
  N11: L298N_Motors_Controller.OUT2, Part3.IN1
  N12: L298N_Motors_Controller.OUT3, Part2.IN2
  N13: L298N_Motors_Controller.OUT4, Part2.IN1
  N14: UBEC_Voltage_Regulator.IN+, 7_4_LiPO_Battery.+, Zero_Bot_Servo_Weapon.vcc
  N15: L298N_Weapon_Controller.OUT3, Weapon_Motor.pin_2
  N16: L298N_Weapon_Controller.OUT4, Weapon_Motor.pin_1

notes:
  Connection for Zero Bot
  Connection for Scorpion Bot

custom parts:
  L298N DC motor driver: 2x DC motor driver with 78M05 positive voltage regulator (7..35 V) L298N: max 46 V, 2 A Set 5 V Enable jumper to enable 5 V regultor (needed for the L298N) and +5 V output at screw terminal or supply external +5 V at screw terminal Set ENA and/or ENB to +5 V to enable motor permanently or supply ENA and/or ENB with PWM signal IN1 and IN2 set rotation directory for motor A (OUT1/OUT2) IN2 and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
  LM2596 step down module: LM2596 DC-DC step down power supply module 3 A.
  TTP223B Capacitive Touch Sensor Module: The TTP223B capacitive touch sensor module uses the TTP223B IC. The appropriate voltage is approximately 2 to 5.5 volts.
